# Fritzing sketch model4BMesafeSensoru (saved by Fritzing 0.9.4)
breadboards: 1

parts:
  Raspberry_Pi_1 = Raspberry Pi 4 [part_number=RPI-4-b]
  HC-SR04_Sensor_1 = HC-SR04 Ultrasonic Distance Sensor
  R1 = Resistor [tolerance=±5% resistance=220 package="0402 [SMD]"]
  R2 = Resistor [tolerance=±5% resistance=220 package="0402 [SMD]"]

nets:
  N1: Raspberry_Pi_1.GPIO24, R1.Pin_1, R2.Pin_1
  N2: Raspberry_Pi_1.GPIO23, HC-SR04_Sensor_1.TRIG
  GND: Raspberry_Pi_1.GND, HC-SR04_Sensor_1.GND, R2.Pin_0
  5V: Raspberry_Pi_1.5V, HC-SR04_Sensor_1.VCC
  N3: HC-SR04_Sensor_1.ECHO, R1.Pin_0

custom parts:
  Raspberry Pi 4: The RPi4, a faster version of the awesome Raspberry Pi 2 B ARM Board with 40 pin gpio. Ready for special Raspberry Pi B+ and RPi2 Hat (Hardware attached (on) top)
